# Fritzing sketch booster (saved by Fritzing 0.9.2b)
breadboards: 1

parts:
  L1 = Inductor [inductance=2.2mH package="400 mil [THT]"]
  Q3 = Basic FET N-Channel [part_number=IRF710 package="TO220 [THT]"]
  Q4 = Basic FET N-Channel [part_number=IRF710 package="TO220 [THT]"]
  Arduino_Uno = Arduino Uno (Rev3)
  L2 = Inductor [package="400 mil [THT]"]
  C1 = Electrolytic Capacitor [capacitance=47µF package="300 mil [THT, electrolytic]"]
  D2 = Rectifier Diode [part_number=1N4007 package="Melf DO-213 AB [SMD]"]
  VCC1 = Battery block 9V [part_number=7.4V]
  Q1 = NPN-Transistor [package="TO92 [THT]"]
  Q2 = NPN-Transistor [package="TO92 [THT]"]
  R2 = Resistor [tolerance=±5% resistance=1k package=THT]
  R3 = Resistor [tolerance=±5% resistance=100k package=THT]
  R4 = Resistor [tolerance=±5% resistance=1k package=THT]
  R1 = Resistor [tolerance=±5% resistance=100k package=THT]
  D1 = Rectifier Diode [part_number=1N4007 package="300 mil [THT]"]

nets:
  N1: L1.pin_0, Arduino_Uno.VIN, VCC1.+, Q1.C, Q2.C
  N2: L1.pin_1, Q3.drain, D1.anode
  N3: Q3.gate, Q1.E, R2.Pin_1
  N4: Q3.source, Q4.source, Arduino_Uno.GND, C1.-, VCC1.-, R2.Pin_0, R3.Pin_0, R4.Pin_0, R1.Pin_0
  N5: Q4.gate, Q2.E, R4.Pin_1
  N6: Q4.drain, L2.pin_1, D2.anode
  N7: Arduino_Uno.D8, Q1.B, R1.Pin_1
  N8: Arduino_Uno.D9_PWM, Q2.B, R3.Pin_1
  N9: L2.pin_0, C1.+, D2.cathode, D1.cathode

notes:
  4 kHz
  92%
  25 Hz
  50%
